# Fritzing sketch GosFridge (saved by Fritzing 0.9.3b)
breadboards: 1

parts:
  Part1 = Adafruit INA219 High Side DC Current Sensor Breakout [part_number="Adafruit #904"]
  Part3 = Real Time Clock Module - DS1307 RTC Breakout Board
  R1 = Resistor [tolerance=±5% resistance=4.7k package="2512 [SMD]"]
  U1 = atmega328 [package=dip]
  Part6 = PowerBoost 1000 Basic
  XTAL1 = Crystal [frequency="16 Mhz" package=SMD]
  C7 = Ceramic Capacitor [capacitance=0.22mF package="0805 [SMD, multilayer]"]
  C8 = Ceramic Capacitor [capacitance=0.22mF package="0805 [SMD, multilayer]"]
  R3 = Resistor [tolerance=±5% resistance=10k package="2512 [SMD]"]
  Part7 = Adafruit Bluefruit EZ-Link [part_number="Adafruit #1588"]
  C10 = Electrolytic Capacitor [capacitance=1μF package="0405 [SMD, electrolytic]"]
  Part8 = Adafruit MicroSD card breakout board [part_number="Adafruit #254"]
  LED1 = smd LED [color="Green (560nm)" package="1206 [SMD]"]
  BAT1 = Battery Holders [package=battery-aa]
  BAT2 = Battery Holders [package=battery-aa]
  BAT3 = Battery Holders [package=battery-aa]
  BAT4 = Battery Holders [package=battery-aa]

nets:
  N1: Part1.VIN-, Part6.VBAT
  N2: Part1.VIN+, BAT4.+
  VCC: Part1.VCC, Part3.5V, R1.Pin_1, U1.VCC, U1.AVCC, U1.AREF, Part6.5.0V, R3.Pin_1, Part7.VIN, Part8.VCC
  GND: Part1.GND, Part3.GND, U1.GND, Part6.GND, C7.0, C8.0, Part7.GND, Part8.GND, LED1.anode, BAT1.-
  N3: Part1.SCL, Part3.SCL, U1.A5
  N4: Part1.SDA, Part3.SDA, U1.A4
  N5: R1.Pin_0, U1.D4
  N6: U1.RESET, R3.Pin_0, Part7.TXD, C10.+
  N7: U1.D0_(RX), Part7.RXD
  N8: U1.XLAT1, XTAL1.pin_0, C7.1
  N9: U1.XLAT2, XTAL1.pin_1, C8.1
  N10: U1.D5_(PWM), LED1.cathode
  N11: U1.D10_(PWM), Part8.CS
  N12: U1.D11_(PWM), Part8.DI
  N13: U1.D12, Part8.DO
  N14: U1.D13, Part8.CLK
  N15: Part7.RTS/DTR, C10.-
  N16: BAT1.+, BAT2.-
  N17: BAT2.+, BAT3.-
  N18: BAT3.+, BAT4.-

notes:
  Batteries. Boosted to 5.2V
  1-[n] DS18B20 Thermometers

custom parts:
  Adafruit INA219 High Side DC Current Sensor Breakout: This breakout board will solve all your power-monitoring problems. Instead of struggling with two multimeters, you can just use the handy INA219B chip on this breakout to both measure both the high side voltage and DC current draw over I2C with 1% precision. Most current-measuring devices such as our current panel meter are only good for low side measuring. That means that unless you want to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
  PowerBoost 1000 Basic: The PowerBoost 1000 is a little DC/DC boost converter module that can run from 1.8V batteries or higher, and convert the battery output to 5.2V DC for running your 5V projects. At its heart is a TPS61030 boost converter from TI. This boost converter chip has some really nice extras such as low battery detection, 4A internal switch, synchronous conversion, excellent efficiency, and 700KHz high-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
  Adafruit Bluefruit EZ-Link: We are excited to add another product to our growing Adafruit Bluefruit line, this time it's the Bluefruit EZ-Link: the best Bluetooth Serial Link device ever made. Like you, we have purchased all sorts of Bluetooth serial link modules, with high expectations - we just wanted something that worked! But nothing ever did exactly what we wanted: there was always some configuration modes to wade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
  Adafruit MicroSD card breakout board: Not just a simple breakout board, this microSD adapter goes the extra mile - designed for ease of use. Onboard 5v->3v regulator provides 150mA for power-hungry cards 3v level shifting means you can use this with ease on either 3v or 5v systems Uses a proper level shifting chip, not resistors: less problems, and faster read/write access Use 3 or 4 digital pins to read and write 2Gb+ of storage!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
